# Fritzing sketch Blinky (saved by Fritzing 0.9.3b)
breadboards: 1

parts:
  Part1 = Adafruit HUZZAH32 ESP32 Feather [part_number="Adafruit #3405"]
  R1 = Resistor [tolerance=±5% resistance=150 package="2512 [SMD]"]
  LED1 = smd LED [color="Red (633nm)" package="0603 [SMD]"]
  S1 = Pushbutton [package="[SMD]"]

nets (from the breadboard view):
  N1: Part1.GND, R1.Pin_1, S1.Pin_3, S1.Pin_4
  N2: Part1.IO32_A7, LED1.anode
  N3: Part1.IO14_A6, S1.Pin_1, S1.Pin_2
  N4: R1.Pin_0, LED1.cathode
