# Fritzing sketch Blinky-traffic-lights (saved by Fritzing 0.9.3b)
breadboards: 1

parts:
  R1 = Resistor [tolerance=±5% resistance=150 package="2512 [SMD]"]
  LED1 = smd LED [color="Red (633nm)" package="0603 [SMD]"]
  S1 = Pushbutton [package="[SMD]"]
  R2 = Resistor [tolerance=±5% resistance=150 package="2512 [SMD]"]
  LED2 = smd LED [color="Yellow (592nm)" package="0603 [SMD]"]
  R3 = Resistor [tolerance=±5% resistance=150 package="2512 [SMD]"]
  LED3 = smd LED [color="Green (555nm)" package="0603 [SMD]"]
  Part1 = Adafruit HUZZAH32 ESP32 Feather [part_number="Adafruit #3405"]

nets (from the breadboard view):
  N1: R1.Pin_0, LED1.cathode
  N2: R1.Pin_1, S1.Pin_3, S1.Pin_4, R2.Pin_1, R3.Pin_1, Part1.GND
  N3: LED1.anode, Part1.IO32_A7
  N4: S1.Pin_1, S1.Pin_2, Part1.IO14_A6
  N5: R2.Pin_0, LED2.cathode
  N6: LED2.anode, Part1.IO15_A8
  N7: R3.Pin_0, LED3.cathode
  N8: LED3.anode, Part1.IO12_A11
