# Fritzing sketch ultrasonic-sensor (saved by Fritzing 0.9.3b)
breadboards: 1

parts:
  Part1 = Adafruit HUZZAH32 ESP32 Feather [part_number="Adafruit #3405"]
  hc-sr1 = hc-sr04

nets (from the schematic view):
  N1: Part1.A2_I34, hc-sr1.Echo
  N2: Part1.A1_DAC1, Part1.VBAT, hc-sr1.Trig
  GND: Part1.GND, hc-sr1.GND
